# Fritzing sketch polaczenie2 (saved by Fritzing 0.9.3b)
breadboards: 1

parts:
  MCU1 = Raspberry Pi Zero
  DS1 = DS18B20 1-Wire Temperature Sensor [part_number=DS18B20]
  R5 = Resistor [tolerance=±5% resistance=220 package=THT]
  Part1 = KY-019 5V Relay Module [package="Breakout board"]  # not connected
  Part2 = KY-019 5V Relay Module [package="Breakout board"]  # not connected
  Part3 = KY-019 5V Relay Module [package="Breakout board"]  # not connected
  Part4 = KY-019 5V Relay Module [package="Breakout board"]  # not connected

nets:
  N1: MCU1.pin_1, MCU1.pin_2, MCU1.pin_3, MCU1.pin_4, MCU1.pin_17, MCU1.pin_18, DS1.VDD, R5.Pin_1
  N2: MCU1.pin_5, MCU1.pin_6, MCU1.pin_9, MCU1.pin_10, MCU1.pin_13, MCU1.pin_14, MCU1.pin_19, MCU1.pin_20, MCU1.pin_25, MCU1.pin_26, MCU1.pin_29, MCU1.pin_30, MCU1.pin_33, MCU1.pin_34, MCU1.pin_39, MCU1.pin_40, DS1.GND
  N3: MCU1.pin_7, MCU1.pin_8, DS1.DQ, R5.Pin_0
  N4: MCU1.pin_11, MCU1.pin_12
  N5: MCU1.pin_15, MCU1.pin_16
  N6: MCU1.pin_21, MCU1.pin_22
  N7: MCU1.pin_23, MCU1.pin_24
  N8: MCU1.pin_27, MCU1.pin_28
  N9: MCU1.pin_31, MCU1.pin_32
  N10: MCU1.pin_35, MCU1.pin_36
  N11: MCU1.pin_37, MCU1.pin_38

custom parts:
  KY-019 5V Relay Module: KY-019 5V Relay module, used to control AC circuits.
